# Fritzing sketch RememberMe (saved by Fritzing 0.9.3b)
breadboards: 1

parts:
  Componente1 = Arduino Uno (Rev3)
  R1 = Trimmer Potentiometer [maximum_resistance=10kΩ package=THT]
  LCD1 = LCD screen
  R4 = Resistor [tolerance=±5% resistance=220 package=THT]
  S1 = Pushbutton [package="[THT]"]
  S2 = Pushbutton [package="[THT]"]
  LED1 = RGB LED (com. cathode, rgb) [package="5 mm [THT]"]  # not connected
  J1 = Piezo Speaker  # not connected
  R5 = Resistor [tolerance=±5% resistance=220 package=THT]
  R6 = Resistor [tolerance=±5% resistance=220 package=THT]
  R7 = Resistor [tolerance=±5% resistance=220 package=THT]
  R8 = Resistor [tolerance=±5% resistance=220 package=THT]

nets:
  N1: Componente1.D8, LCD1.E
  N2: Componente1.D9_PWM, LCD1.DB4
  N3: Componente1.D10_PWM/SS, LCD1.DB5
  N4: Componente1.D11_PWM/MOSI, LCD1.DB6
  N5: Componente1.D12/MISO, LCD1.DB7
  GND: Componente1.GND, R1.leg2, LCD1.VSS, LCD1.R/W, LCD1.LED-, R6.Pin_1
  N6: Componente1.D2, S2.Pin_1, S2.Pin_2, R5.Pin_1
  N7: Componente1.D3_PWM, S1.Pin_3, S1.Pin_4, R6.Pin_0
  N8: Componente1.D4, R4.Pin_0, R4.Pin_1
  N9: Componente1.D5_PWM, R7.Pin_0, R7.Pin_1
  N10: Componente1.D6_PWM, R8.Pin_0, R8.Pin_1
  N11: Componente1.D7, LCD1.RS
  5V: Componente1.5V, R1.leg1, LCD1.VDD, LCD1.LED+, S1.Pin_1, S1.Pin_2, S2.Pin_3, S2.Pin_4, R5.Pin_0
  N12: R1.wiper, LCD1.V0
